# Fritzing sketch TFG_Prototype_sensor_refactor (saved by Fritzing 1.0.1rc)
breadboards: 1

parts:
  Mod1 = Heltec WiFi LoRa 32 V2 [part_number=HTIT-WB32LA]
  Componente6 = Adafruit Ultimate GPS v3 [part_number="Adafruit #746"]
  DHT3 = Humidity and Temperature Sensor DHT11
  Componente7 = InvenSense MPU6050
  Componente8 = GY-VL53L0XV2 Laser Ranger Module

nets:
  N1: Mod1.pin_7, DHT3.Data-signal
  N2: Mod1.pin_16, Mod1.pin_17
  GND: Mod1.GND, Componente6.GND, DHT3.GND_1, Componente7.GND, Componente8.GND
  VCC: Mod1.pin_20, Componente6.VIN, DHT3.Vcc, Componente7.VCC, Componente8.VCC
  N3: Mod1.pin_21, Mod1.pin_22
  N4: Mod1.pin_23, Componente6.RX
  N5: Mod1.pin_24, Componente6.TX
  N6: Mod1.pin_32, Componente7.SDA, Componente8.SDA
  N7: Mod1.pin_34, Componente7.SCL, Componente8.SCL

custom parts:
  Adafruit Ultimate GPS v3: We carry a few different GPS modules here in the Adafruit shop, but none that satisfied our every desire - that's why we designed this little GPS breakout board. We believe this is the Ultimate GPS module, so we named it that. It's got everything you want and more: -165 dBm sensitivity, 10 Hz updates, 66 channels 5V friendly design and only 20mA current draw Breadboard friendly + two mounting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
  Humidity and Temperature Sensor DHT11: Digital relative humidity & temperature sensor DHT11
  GY-VL53L0XV2 Laser Ranger Module: The GY-VL53L0XV2 is based on the VL53L0X from ST Microelectronics, a time-of-flight ranging system integrated into a compact module.
